# Fritzing sketch resnet_board (saved by Fritzing 0.8.7b)
circuit board: 4.9628cm x 4.28325cm
breadboards: 1

parts:
  J1 = screw terminal, 3 pins
  J5 = Screw terminal - 2 pins [package=THT]
  R1 = Resistor [tolerance=±5% resistance=33 package=THT]
  R2 = Resistor [tolerance=±5% resistance=33 package=THT]
  R3 = Resistor [tolerance=±5% resistance=33 package=THT]
  R4 = Resistor [tolerance=±5% resistance=33 package=THT]
  R5 = Resistor [tolerance=±5% resistance=33 package=THT]
  R6 = Resistor [tolerance=±5% resistance=33 package=THT]
  R7 = Resistor [tolerance=±5% resistance=33 package=THT]
  R8 = Resistor [tolerance=±5% resistance=33 package=THT]
  JP1 = male pin header, 2 pins [form="♂ (male)"]
  JP2 = male pin header, 2 pins [form="♂ (male)"]
  J6 = Screw terminal - 2 pins [package=THT]
  J2 = screw terminal, 3 pins
  R9 = Resistor [tolerance=±5% resistance=33 package=THT]
  R10 = Resistor [tolerance=±5% resistance=33 package=THT]
  R11 = Resistor [tolerance=±5% resistance=33 package=THT]
  R12 = Resistor [tolerance=±5% resistance=33 package=THT]
  R13 = Resistor [tolerance=±5% resistance=33 package=THT]
  R14 = Resistor [tolerance=±5% resistance=33 package=THT]
  R15 = Resistor [tolerance=±5% resistance=33 package=THT]
  R16 = Resistor [tolerance=±5% resistance=33 package=THT]
  JP3 = male pin header, 2 pins [form="♂ (male)"]
  JP4 = male pin header, 2 pins [form="♂ (male)"]
  J7 = Screw terminal - 2 pins [package=THT]
  J3 = screw terminal, 3 pins
  R17 = Resistor [tolerance=±5% resistance=33 package=THT]
  R18 = Resistor [tolerance=±5% resistance=33 package=THT]
  R19 = Resistor [tolerance=±5% resistance=33 package=THT]
  R20 = Resistor [tolerance=±5% resistance=33 package=THT]
  R21 = Resistor [tolerance=±5% resistance=33 package=THT]
  R22 = Resistor [tolerance=±5% resistance=33 package=THT]
  R23 = Resistor [tolerance=±5% resistance=33 package=THT]
  R24 = Resistor [tolerance=±5% resistance=33 package=THT]
  JP5 = male pin header, 2 pins [form="♂ (male)"]
  JP6 = male pin header, 2 pins [form="♂ (male)"]
  J8 = Screw terminal - 2 pins [package=THT]
  J4 = screw terminal, 3 pins
  R25 = Resistor [tolerance=±5% resistance=33 package=THT]
  R26 = Resistor [tolerance=±5% resistance=33 package=THT]
  R27 = Resistor [tolerance=±5% resistance=33 package=THT]
  R28 = Resistor [tolerance=±5% resistance=33 package=THT]
  R29 = Resistor [tolerance=±5% resistance=33 package=THT]
  R30 = Resistor [tolerance=±5% resistance=33 package=THT]
  R31 = Resistor [tolerance=±5% resistance=33 package=THT]
  R32 = Resistor [tolerance=±5% resistance=33 package=THT]
  JP7 = male pin header, 2 pins [form="♂ (male)"]
  JP8 = male pin header, 2 pins [form="♂ (male)"]

nets:
  N1: J1.pin1, R1.Pin_1, R2.Pin_1, R3.Pin_1, R4.Pin_1
  N2: J5.pin1, R7.Pin_0, R8.Pin_0
  N3: R1.Pin_0, R5.Pin_1, JP1.pin1
  N4: R2.Pin_0, R6.Pin_1, JP1.pin2
  N5: R3.Pin_0, R7.Pin_1, JP2.pin1
  N6: R4.Pin_0, R8.Pin_1, JP2.pin2
  N7: J6.pin1, R9.Pin_0, R12.Pin_0
  N8: J2.pin1, R10.Pin_1, R11.Pin_1, R14.Pin_1, R16.Pin_1
  N9: R9.Pin_1, R11.Pin_0, JP4.pin1
  N10: R10.Pin_0, R15.Pin_1, JP3.pin2
  N11: R12.Pin_1, R16.Pin_0, JP4.pin2
  N12: R13.Pin_1, R14.Pin_0, JP3.pin1
  N13: J7.pin1, R17.Pin_0, R20.Pin_0
  N14: J3.pin1, R18.Pin_1, R19.Pin_1, R22.Pin_1, R24.Pin_1
  N15: R17.Pin_1, R19.Pin_0, JP6.pin1
  N16: R18.Pin_0, R23.Pin_1, JP5.pin2
  N17: R20.Pin_1, R24.Pin_0, JP6.pin2
  N18: R21.Pin_1, R22.Pin_0, JP5.pin1
  N19: J8.pin1, R25.Pin_0, R28.Pin_0
  N20: J4.pin1, R26.Pin_1, R27.Pin_1, R30.Pin_1, R32.Pin_1
  N21: R25.Pin_1, R27.Pin_0, JP8.pin1
  N22: R26.Pin_0, R31.Pin_1, JP7.pin2
  N23: R28.Pin_1, R32.Pin_0, JP8.pin2
  N24: R29.Pin_1, R30.Pin_0, JP7.pin1

notes:
  Resitors
  Arnau (OSL)
  network PCB
  June, 2014
